# Fritzing sketch LED_Limiter (saved by Fritzing 0.9.2b)
breadboards: 1

parts:
  R1 = Resistor [tolerance=±5% resistance=470 package=THT]
  LED1 = LED - 5mm [color="Red (633nm)" package="5 mm [THT]"]
  LED2 = LED - 5mm [color="Red (633nm)" package="5 mm [THT]"]
  J1 = female pin header, 1 pin [form="♀ (female)"]
  R2 = Resistor [tolerance=±5% resistance=15k package=THT]
  J2 = female pin header, 1 pin [form="♀ (female)"]
  R3 = Resistor [tolerance=±5% resistance=470 package=THT]
  R4 = Resistor [tolerance=±5% resistance=470 package=THT]
  R5 = Resistor [tolerance=±5% resistance=470 package=THT]

nets:
  N1: R1.Pin_0, J1.pin1, R3.Pin_0, R4.Pin_0, R5.Pin_0
  N2: R1.Pin_1, LED1.anode, LED2.cathode, R2.Pin_0, J2.pin1, R3.Pin_1, R4.Pin_1, R5.Pin_1
  N3: LED1.cathode, LED2.anode, R2.Pin_1
