# Fritzing sketch Limiter (saved by Fritzing 0.9.2b)
breadboards: 1

parts:
  D1 = Zener Diode [part_number=1N4732A breakdown_voltage=3.6V package="Melf DO-213 AB [SMD]"]
  D2 = Zener Diode [part_number=1N4732A breakdown_voltage=3.6V package="Melf DO-213 AB [SMD]"]
  R1 = Resistor [tolerance=±5% resistance=1k package=THT]
  J1 = female pin header, 1 pin [form="♀ (female)"]
  J2 = female pin header, 1 pin [form="♀ (female)"]

nets:
  N1: D1.cathode, R1.Pin_1, J2.pin1
  N2: D1.anode, D2.anode
  N3: R1.Pin_0, J1.pin1
