# Fritzing sketch LED_Limiter_ケース内配線 (saved by Fritzing 0.9.2b)
perfboards: 1

parts:
  R1 = Rotary Potentiometer (Small) [maximum_resistance=100kΩ package=THT]
  R2 = Rotary Potentiometer (Small) [maximum_resistance=100kΩ package=THT]
  TRS1 = Audio Jack (TRS) 3.5mm [package="PG203J [THT]"]
  TRS2 = Audio Jack (TRS) 3.5mm [package="PG203J [THT]"]
  TRS3 = Audio Jack (TRS) 3.5mm [package="PG203J [THT]"]
  S1 = Toggle Switch [package=THT]
  S2 = Toggle Switch [package=THT]
  J1 = female pin header, 3 pins [form="♀ (female)"]
  J2 = female pin header, 2 pins [form="♀ (female)"]
  J3 = female pin header, 2 pins [form="♀ (female)"]
  J4 = female pin header, 3 pins [form="♀ (female)"]
  J5 = female pin header, 3 pins [form="♀ (female)"]

nets:
  N1: R1.leg1, R2.leg1, TRS1.Sleeve, J1.pin3
  N2: R1.wiper, J1.pin2
  N3: R1.leg2, TRS1.Tip
  N4: R2.wiper, J1.pin1
  N5: R2.leg2, TRS1.Ring
  N6: TRS2.Sleeve, J2.pin1
  N7: TRS2.Tip, J2.pin2
  N8: TRS3.Sleeve, J3.pin1
  N9: TRS3.Ring, J3.pin2
  N10: S1.L1, J4.pin1
  N11: S1.COM, J4.pin3
  N12: S1.L2, J4.pin2
  N13: S2.L1, J5.pin1
  N14: S2.COM, J5.pin3
  N15: S2.L2, J5.pin2

notes:
  Stereo3.5mm
  Mono6.3mm
  DPDT
  Dual POT
